// Logisim project ktmt_project.circ as structural Verilog: 6 circuits, main circuit full adder
module full_adder (
  input  Cin,
  input  A,
  input  B,
  output S,
  output Cout
);

  wire and_1_out, and_2_out, xor_1_out;

  xor xor_1 (xor_1_out, A, B);
  xor xor_2 (S, xor_1_out, Cin);
  and and_1 (and_1_out, Cin, xor_1_out);
  and and_2 (and_2_out, B, A);
  or or_1 (Cout, and_1_out, and_2_out);
endmodule

module _4bit_ripple_adder (
  input  [3:0] A,
  input  [3:0] B,
  output [3:0] sum,
  output overflow
);

  wire full_adder_1_cout, full_adder_2_cout, full_adder_3_cout;

  full_adder full_adder_1 (.Cin(1'b0), .A(A[0]), .B(B[0]), .S(sum[0]), .Cout(full_adder_1_cout));
  full_adder full_adder_2 (.Cin(full_adder_1_cout), .A(A[1]), .B(B[1]), .S(sum[1]), .Cout(full_adder_2_cout));
  full_adder full_adder_3 (.Cin(full_adder_2_cout), .A(A[2]), .B(B[2]), .S(sum[2]), .Cout(full_adder_3_cout));
  full_adder full_adder_4 (.Cin(full_adder_3_cout), .A(A[3]), .B(B[3]), .S(sum[3]), .Cout(overflow));

  // Notes on the sheet:
  //   LSB
  //   MSB
endmodule

module _7_bit_ripple_adder (
  input  [6:0] A,
  input  [6:0] B,
  output [6:0] sum,
  output overflow
);

  wire full_adder_1_cout, full_adder_2_cout, full_adder_3_cout, full_adder_4_cout, full_adder_5_cout,
       full_adder_6_cout;

  full_adder full_adder_1 (.Cin(1'b0), .A(A[0]), .B(B[0]), .S(sum[0]), .Cout(full_adder_1_cout));
  full_adder full_adder_2 (.Cin(full_adder_1_cout), .A(A[1]), .B(B[1]), .S(sum[1]), .Cout(full_adder_2_cout));
  full_adder full_adder_3 (.Cin(full_adder_2_cout), .A(A[2]), .B(B[2]), .S(sum[2]), .Cout(full_adder_3_cout));
  full_adder full_adder_4 (.Cin(full_adder_3_cout), .A(A[3]), .B(B[3]), .S(sum[3]), .Cout(full_adder_4_cout));
  full_adder full_adder_5 (.Cin(full_adder_4_cout), .A(A[4]), .B(B[4]), .S(sum[4]), .Cout(full_adder_5_cout));
  full_adder full_adder_6 (.Cin(full_adder_5_cout), .A(A[5]), .B(B[5]), .S(sum[5]), .Cout(full_adder_6_cout));
  full_adder full_adder_7 (.Cin(full_adder_6_cout), .A(A[6]), .B(B[6]), .S(sum[6]), .Cout(overflow));

  // Notes on the sheet:
  //   LSB
  //   MSB
endmodule

module _6_y (
  input  [3:0] y__4_bit,
  output [6:0] _6_y,
  output Check_overflow
);

  wire _7_bit_adder_2_overflow, _7_bit_adder_3_overflow, _7_bit_adder_4_overflow, _7_bit_adder_5_overflow,
       _7_bit_adder_overflow;
  wire [3:0] adder_1_out;
  wire [6:0] _7_bit_adder_2_sum, _7_bit_adder_3_sum, _7_bit_adder_4_sum, _7_bit_adder_sum, bit_extender_1_out;

  Adder #(.width(4)) adder_1 (.a(4'b0000), .b(y__4_bit), .out(adder_1_out));  // open: cin, cout
  assign bit_extender_1_out = {{3{1'b0}}, adder_1_out};  // Bit_Extender bit_extender_1
  _7_bit_ripple_adder _7_bit_adder (
    .A(bit_extender_1_out), .B(bit_extender_1_out), .sum(_7_bit_adder_sum), .overflow(_7_bit_adder_overflow));
  _7_bit_ripple_adder _7_bit_adder_2 (
    .A(bit_extender_1_out), .B(bit_extender_1_out), .sum(_7_bit_adder_2_sum),
    .overflow(_7_bit_adder_2_overflow));
  _7_bit_ripple_adder _7_bit_adder_3 (
    .A(bit_extender_1_out), .B(bit_extender_1_out), .sum(_7_bit_adder_3_sum),
    .overflow(_7_bit_adder_3_overflow));
  _7_bit_ripple_adder _7_bit_adder_4 (
    .A(_7_bit_adder_sum), .B(_7_bit_adder_2_sum), .sum(_7_bit_adder_4_sum), .overflow(_7_bit_adder_4_overflow));
  _7_bit_ripple_adder _7_bit_adder_5 (
    .A(_7_bit_adder_4_sum), .B(_7_bit_adder_3_sum), .sum(_6_y), .overflow(_7_bit_adder_5_overflow));
  or or_1 (Check_overflow, _7_bit_adder_3_overflow, _7_bit_adder_2_overflow, _7_bit_adder_overflow, _7_bit_adder_5_overflow, _7_bit_adder_4_overflow);
endmodule

module _6_y_8 (
  input  [3:0] y__4_bit,
  output [6:0] _6_y_8,
  output Check_negative,
  output Check_overflow
);

  wire [6:0] n6_y_1__6_y;

  _6_y u_6_y_1 (.y__4_bit(y__4_bit), .Check_overflow(Check_overflow), ._6_y(n6_y_1__6_y));
  Subtractor #(.width(7)) subtractor_1 (
    .a(n6_y_1__6_y), .b(7'b0001000), .out(_6_y_8), .bout(Check_negative));  // open: bin

  // Notes on the sheet:
  //   6*y
endmodule

module _6_y_8_x (
  input  [3:0] y__4_bit,
  input  [3:0] x__4_bit,
  output Check_negative,
  output [6:0] f_x_y__6_y_8_x,
  output Check_overflow,
  output Check_overflow_2
);

  wire [3:0] adder_1_out;
  wire [6:0] bit_extender_1_out, n6_y_8_1__6_y_8;

  Adder #(.width(4)) adder_1 (.a(4'b0000), .b(x__4_bit), .out(adder_1_out));  // open: cin, cout
  _6_y_8 u_6_y_8_1 (
    .y__4_bit(y__4_bit), ._6_y_8(n6_y_8_1__6_y_8), .Check_negative(Check_negative),
    .Check_overflow(Check_overflow));
  assign bit_extender_1_out = {{3{1'b0}}, adder_1_out};  // Bit_Extender bit_extender_1
  _7_bit_ripple_adder u_7_bit_ripple_adder_1 (
    .A(n6_y_8_1__6_y_8), .B(bit_extender_1_out), .sum(f_x_y__6_y_8_x), .overflow(Check_overflow_2));

  // Notes on the sheet:
  //   6*y-8
  //    7 bit adder
endmodule
